# Fritzing sketch circuit_diagram_frizing (saved by Fritzing 0.9.3b)
breadboards: 1

parts:
  W1 = ESPr Developer [package="DIP (Dual Inline) [THT]"]
  LED1 = LED - 5mm [color="Red (633nm)" package="5 mm [THT]"]
  R1 = Resistor [tolerance=±5% resistance=10 package=THT]

nets:
  GND: W1.GND, W1.VIN, LED1.cathode
  N1: W1.IO5, R1.Pin_1
  N2: LED1.anode, R1.Pin_0
